# Fritzing sketch ESP32C3SM_LD2420 (saved by Fritzing 1.0.4)
circuit board: 4.29836cm x 4.64726cm

parts:
  AC = Screw terminal - 2 pins [package=THT]
  Esp32c3_Super_Mini = Esp32-c3 super mini
  HLK-PM1 = HLK-PM01
  HLK-LD2420 = HLK-LD2420

nets:
  N1: AC.pin1, HLK-PM1.AC#1
  N2: AC.pin2, HLK-PM1.AC#0
  N3: Esp32c3_Super_Mini.Pin_2, HLK-LD2420.Pin_3
  N4: Esp32c3_Super_Mini.Pin_3, HLK-LD2420.Pin_4
  N5: Esp32c3_Super_Mini.Pin_14, HLK-LD2420.Pin_1
  N6: Esp32c3_Super_Mini.Pin_15, HLK-PM1.-Vo, HLK-LD2420.Pin_2
  N7: Esp32c3_Super_Mini.Pin_16, HLK-PM1.+Vo

custom parts:
  Esp32-c3 super mini: ESP32-C3 Development Board ESP32 SuperMini Development Board ESP32 Development Board WiFi Bluetooth.
  HLK-LD2420: HLK-LD2420 is mainly used to detect whether there is movement or slight movement of the human body in the indoor scene perception area.
